// Digital circuit twoBitReg.dig as structural Verilog
module twoBitReg (
  input  [1:0] in,
  input  enable,
  input  clk,
  input  clr,
  output [1:0] out
);

  wire [1:0] twobitbusmux_1_y;

  twoBitBusMux twobitbusmux_1 (.a(out), .b(in), .sel(enable), .y(twobitbusmux_1_y));
  D_FF_AS d_ff_as_1 (.Set(1'b0), .D(twobitbusmux_1_y[0]), .C(clk), .Clr(clr), .Q(out[0]));  // open: nQ
  D_FF_AS d_ff_as_2 (.Set(1'b0), .D(twobitbusmux_1_y[1]), .C(clk), .Clr(clr), .Q(out[1]));  // open: nQ
endmodule
