// Digital circuit controller.dig as structural Verilog
module controller (
  input  clk,
  input  clr,
  input  [15:0] data__in,
  input  load__ir,
  output [9:0] control
);

  wire [1:0] step__reg;
  wire [13:10] rom__out;
  wire [15:0] instr__reg;

  sixteenBitReg sixteenbitreg_1 (.in(data__in), .sel(load__ir), .clr(clr), .clk(clk), .out(instr__reg));
  // twoBitReg twobitreg_1: pin names not known; wires that end beside it: rom__out[13:12], 1'b1, clr, clk, step__reg
  ROM #(.AddrBits(18), .Bits(14)) microcode_ROM (.A({instr__reg, step__reg}), .sel(1'b1), .D({rom__out, control}));

  // Other names for the same wires on the sheet: rom__out[9:0] = control

  // Notes on the sheet:
  //   contents of microcode_ROM (hex, n*v repeats v):
  //   1205,234,0,0,1205,294,0,0,1205,1000,0,0,1205,0,0,0,1205,0,0,0
  //   ,1205,0,0,0,1205,0,0,0,1205,0,0,3fff
endmodule
