// Digital circuit microprocessor.dig as structural Verilog
module microprocessor (
  input  clk,
  input  [15:0] in,
  input  reset,
  output [15:0] accum
);

  wire [9:0] controller_1_p4;
  wire [15:0] addressgen_1_addr_out, controller_1_p3;

  addressGen addressgen_1 (
    .data_in(controller_1_p3), .clk(clk), .clr(reset), .use__pc(controller_1_p4[9]),
    .load__mar(controller_1_p4[8]), .addr_out(addressgen_1_addr_out));
  // controller controller_1: pin names not known; wires that end beside it: clk, reset, controller_1_p3, controller_1_p4[0], controller_1_p4
  sixteenBitBrainless sixteenbitbrainless_1 (
    .addr__bus(addressgen_1_addr_out), .data_in(in), .arith(controller_1_p4[7]), .invert(controller_1_p4[6]),
    .pass(controller_1_p4[5]), .load__accum(controller_1_p4[4]), .accum__gt_bus(controller_1_p4[3]),
    .write(controller_1_p4[2]), .read(controller_1_p4[1]), .clk(clk), .clr(reset), .accum(accum),
    .data_bus(controller_1_p3));
endmodule
